// Logisim project parte1_cache.circ as structural Verilog: 2 circuits, main circuit main
module main (
  input  RESET_CONT,
  input  [5:0] ENDERECO,
  input  RESET,
  input  CLK,
  output OFFSET,
  output out_6
);

  wire and_1_out, and_2_out, and_3_out, and_4_out, and_5_out, and_6_out, d_ff_1_q, d_ff_2_q, d_ff_3_q,
       d_ff_4_q, decoder_1_out0, decoder_1_out1, decoder_1_out2, decoder_1_out3, multiplexer_1_out,
       multiplexer_2_out, multiplexer_3_out, multiplexer_4_out, multiplexer_5_out, not_1_out, not_2_out,
       not_3_out, not_4_out, not_5_out, not_6_out, not_7_out, not_8_out, or_1_out, or_2_out, or_3_out,
       or_4_out;
  wire [2:0] MEMORIA_TAG_dout;
  wire [3:0] counter_1_q;

  Multiplexer multiplexer_1 (.in0(d_ff_1_q), .in1(1'b1), .out(multiplexer_1_out), .sel(decoder_1_out0));
  Multiplexer multiplexer_2 (.in0(d_ff_2_q), .in1(1'b1), .out(multiplexer_2_out), .sel(decoder_1_out1));
  Multiplexer multiplexer_3 (.in0(d_ff_3_q), .in1(1'b1), .out(multiplexer_3_out), .sel(decoder_1_out2));
  Multiplexer multiplexer_4 (.in0(d_ff_4_q), .in1(1'b1), .out(multiplexer_4_out), .sel(decoder_1_out3));
  D_Flip_Flop d_ff_1 (.D(multiplexer_1_out), .clk(CLK), .Q(d_ff_1_q), .reset(RESET));  // open: Qn, preset
  D_Flip_Flop d_ff_2 (.D(multiplexer_2_out), .clk(CLK), .Q(d_ff_2_q), .reset(RESET));  // open: Qn, preset
  D_Flip_Flop d_ff_3 (.D(multiplexer_3_out), .clk(CLK), .Q(d_ff_3_q), .reset(RESET));  // open: Qn, preset
  D_Flip_Flop d_ff_4 (.D(multiplexer_4_out), .clk(CLK), .Q(d_ff_4_q), .reset(RESET));  // open: Qn, preset
  RAM #(.addrWidth(2), .dataWidth(3)) MEMORIA_TAG (
    .addr(ENDERECO[2:1]), .we(not_1_out), .oe(1'b1), .clk(CLK), .din(ENDERECO[5:3]), .dout(MEMORIA_TAG_dout));
  not not_1 (not_1_out, out_6);
  Multiplexer #(.select(2)) multiplexer_5 (
    .in0(d_ff_1_q), .in1(d_ff_2_q), .in2(d_ff_3_q), .in3(d_ff_4_q), .out(multiplexer_5_out),
    .sel(ENDERECO[2:1]));
  LED OFFSET_LED (.in(ENDERECO[0]));
  Decoder #(.enable("false"), .select(2)) decoder_1 (
    .out0(decoder_1_out0), .out1(decoder_1_out1), .out2(decoder_1_out2), .out3(decoder_1_out3),
    .sel(ENDERECO[2:1]));
  not not_2 (not_2_out, ENDERECO[3]);
  and and_1 (and_1_out, not_2_out, MEMORIA_TAG_dout[0]);
  not not_3 (not_3_out, MEMORIA_TAG_dout[0]);
  and and_2 (and_2_out, not_3_out, ENDERECO[3]);
  not not_4 (not_4_out, ENDERECO[4]);
  and and_3 (and_3_out, not_4_out, MEMORIA_TAG_dout[1]);
  not not_5 (not_5_out, MEMORIA_TAG_dout[1]);
  and and_4 (and_4_out, not_5_out, ENDERECO[4]);
  not not_6 (not_6_out, ENDERECO[5]);
  and and_5 (and_5_out, not_6_out, MEMORIA_TAG_dout[2]);
  not not_7 (not_7_out, MEMORIA_TAG_dout[2]);
  and and_6 (and_6_out, not_7_out, ENDERECO[5]);
  or or_1 (or_1_out, and_1_out, and_2_out);
  or or_2 (or_2_out, and_3_out, and_4_out);
  or or_3 (or_3_out, and_5_out, and_6_out);
  LED led_1 (.in(out_6));
  or or_4 (or_4_out, or_1_out, or_2_out, or_3_out);
  not not_8 (not_8_out, or_4_out);
  Counter #(.max('hf), .width(4)) counter_1 (
    .clr(RESET_CONT), .clk(out_6), .Q(counter_1_q));  // open: load, up, count, D, carry
  and and_7 (out_6, not_8_out, multiplexer_5_out);
  Hex_Digit_Display hex_digit_display_1 (.value(counter_1_q));  // open: dp

  assign OFFSET = ENDERECO[0];

  // Notes on the sheet:
  //   CONSTANTE 1
  //   BIT DE VALIDAÇÃO DE 4 LINHAS
  //   DESLOCAMENTO A0
  //   INDEX A2-A1
  //   TAG A5-A3
  //   BIT DE VALIDADE
  //   T0-T1-T2
  //   S0-S1-S2
  //   PORTA XOR SINTETIZADAS T0,T1,T2 - S0,S1,S2
  //   ACERTO
endmodule

module flip_flops_vs1 (
  input  in_1,
  input  in_2,
  input  in_3,
  input  [5:0] in_4,
  input  in_5,
  input  in_6,
  output out_7
);

  wire d_ff_1_q, d_ff_2_q, d_ff_3_q, d_ff_4_q;

  D_Flip_Flop d_ff_1 (.D(1'b1), .clk(in_2), .Q(d_ff_1_q), .reset(in_1));  // open: Qn, preset
  D_Flip_Flop d_ff_2 (.D(1'b1), .clk(in_2), .Q(d_ff_2_q), .reset(in_1));  // open: Qn, preset
  D_Flip_Flop d_ff_3 (.D(1'b1), .clk(in_2), .Q(d_ff_3_q), .reset(in_1));  // open: Qn, preset
  D_Flip_Flop d_ff_4 (.D(1'b1), .clk(in_2), .Q(d_ff_4_q), .reset(in_1));  // open: Qn, preset
  Multiplexer #(.select(2)) multiplexer_1 (
    .in0(d_ff_1_q), .in1(d_ff_2_q), .in2(d_ff_3_q), .in3(d_ff_4_q));  // open: out, sel
  main main_1 (.RESET_CONT(in_3), .ENDERECO(in_4), .RESET(in_5), .CLK(in_6), .OFFSET(out_7));  // open: out_6
endmodule
