// Logisim project parte2_cabeada.circ as structural Verilog: 1 circuit, main circuit parte2_cabeada
module parte2_cabeada (
  input  CLOCK,
  input  OpCode,
  output PCWrite,
  output PCWrietCond,
  output PCSource,
  output MemRead,
  output IRWRite,
  output RegWrite,
  output ALUSourceA,
  output [1:0] ALUSourceB,
  output [1:0] ALUOp
);

  wire and_1_out, and_2_out, and_3_out, and_4_out, and_5_out, and_6_out, and_8_out, and_9_out, d_ff_1_q,
       d_ff_1_qn, d_ff_2_q, d_ff_3_q, or_1_out, or_2_out, or_3_out, or_4_out, or_5_out, or_6_out, or_7_out,
       or_8_out, or_9_out, or_10_out;
  wire [1:0] and_12_out, and_13_out, and_14_out, and_15_out, bit_extender_1_out, bit_extender_2_out,
       bit_extender_3_out, bit_extender_4_out;

  D_Flip_Flop d_ff_1 (.D(d_ff_1_qn), .clk(CLOCK), .Q(d_ff_1_q), .Qn(d_ff_1_qn), .reset(or_2_out));  // open: preset
  and and_1 (and_1_out, d_ff_2_q, ~d_ff_1_q);  // AND_Gate
  and and_2 (and_2_out, d_ff_1_q, ~d_ff_2_q);  // AND_Gate
  or or_1 (or_1_out, and_1_out, and_2_out);
  D_Flip_Flop d_ff_2 (.D(and_3_out), .clk(CLOCK), .Q(d_ff_2_q), .reset(or_2_out));  // open: Qn, preset
  and and_3 (and_3_out, or_1_out, ~OpCode);  // AND_Gate
  and and_4 (and_4_out, d_ff_1_q, d_ff_3_q);
  and and_5 (and_5_out, d_ff_2_q, d_ff_3_q);
  or or_2 (or_2_out, and_4_out, and_5_out);
  and and_6 (and_6_out, and_8_out, OpCode);
  or or_3 (or_3_out, d_ff_3_q, and_6_out);
  D_Flip_Flop d_ff_3 (.D(or_3_out), .clk(CLOCK), .Q(d_ff_3_q), .reset(or_2_out));  // open: Qn, preset
  and and_7 (IRWRite, ~d_ff_3_q, ~d_ff_2_q, ~d_ff_1_q);  // AND_Gate
  and and_8 (and_8_out, ~d_ff_3_q, ~d_ff_2_q, d_ff_1_q);  // AND_Gate
  or or_4 (or_4_out, IRWRite, and_8_out, RegWrite, PCSource);
  or or_5 (or_5_out, IRWRite, and_9_out, RegWrite);
  or or_6 (or_6_out, and_9_out, IRWRite);
  and and_9 (and_9_out, ~d_ff_3_q, d_ff_2_q, ~d_ff_1_q);  // AND_Gate
  or or_7 (or_7_out, and_9_out, IRWRite, RegWrite);
  _7_Segment_Display u_7_segment_display_1 (
    .g(or_10_out), .f(or_9_out), .a(or_7_out), .b(or_8_out), .e(or_6_out), .d(or_5_out), .c(or_4_out));  // open: dp
  and and_10 (RegWrite, ~d_ff_3_q, d_ff_2_q, d_ff_1_q);  // AND_Gate
  or or_8 (or_8_out, IRWRite, and_8_out, and_9_out, RegWrite, PCSource);
  or or_9 (or_9_out, IRWRite, PCSource);
  or or_10 (or_10_out, and_9_out, RegWrite, PCSource);
  and and_11 (PCSource, d_ff_3_q, ~d_ff_2_q, ~d_ff_1_q);  // AND_Gate
  assign bit_extender_1_out = {{1{and_9_out}}, and_9_out};  // Bit_Extender bit_extender_1
  or or_11 (ALUSourceA, and_9_out, PCSource);
  assign bit_extender_2_out = {{1{IRWRite}}, IRWRite};  // Bit_Extender bit_extender_2
  assign bit_extender_3_out = {{1{and_8_out}}, and_8_out};  // Bit_Extender bit_extender_3
  assign bit_extender_4_out = {{1{PCSource}}, PCSource};  // Bit_Extender bit_extender_4
  assign and_12_out = bit_extender_2_out & 2'b01;  // AND_Gate and_12, 2 bits wide
  assign ALUSourceB = and_12_out | and_13_out;  // OR_Gate or_12, 2 bits wide
  assign and_13_out = bit_extender_3_out & 2'b10;  // AND_Gate and_13, 2 bits wide
  assign and_14_out = bit_extender_4_out & 2'b01;  // AND_Gate and_14, 2 bits wide
  assign and_15_out = bit_extender_1_out & 2'b10;  // AND_Gate and_15, 2 bits wide
  assign ALUOp = and_14_out | and_15_out;  // OR_Gate or_13, 2 bits wide

  assign MemRead = IRWRite;
  assign PCWrietCond = PCSource;
  assign PCWrite = IRWRite;

  // Notes on the sheet:
  //   Contador
  //   D0 = -Q0
  //   D1 = (Q0 XOR Q1) AND -OP
  //   D2 = (OP AND S1) OR Q2
  //   RESET = Q2 AND (Q0 OR Q1)
  //   Máquina de estados
  //   Q0,Q1,Q2
  //   S0,S1,S2,S3,S4
endmodule
